# Fritzing sketch Indoor Unit Fritzing (saved by Fritzing 0.9.10b)
breadboards: 2

parts:
  LCM1602_IIC1 = LCM1602 IIC [part_number="LCM1602 IIC" chip_label="LCM1602 IIC" package="DIP (Dual Inline) [THT]"]
  U1 = LuaNode32 / ESP32 [part_number=ESP32S-PIN30]
  NodeMCU = Amica NodeMCU DEVKIT 1.0
  I2C_LCD_Display = LCD screen
  Fan_Representer = LED - 5mm [color="Red (633nm)" current=0.030 package="5 mm [THT]"]
  R1 = Resistor [tolerance=±5% power=0.25 resistance=220 package=THT]

nets:
  VSS: LCM1602_IIC1.VSS, I2C_LCD_Display.VSS
  VDD: LCM1602_IIC1.VDD, I2C_LCD_Display.VDD
  N1: LCM1602_IIC1.V0, I2C_LCD_Display.V0
  N2: LCM1602_IIC1.RS, I2C_LCD_Display.RS
  N3: LCM1602_IIC1.RW, I2C_LCD_Display.R/W
  N4: LCM1602_IIC1.E, I2C_LCD_Display.E
  N5: LCM1602_IIC1.D0, I2C_LCD_Display.DB0
  N6: LCM1602_IIC1.D1, I2C_LCD_Display.DB1
  N7: LCM1602_IIC1.D2, I2C_LCD_Display.DB2
  N8: LCM1602_IIC1.D3, I2C_LCD_Display.DB3
  N9: LCM1602_IIC1.D4, I2C_LCD_Display.DB4
  N10: LCM1602_IIC1.D5, I2C_LCD_Display.DB5
  N11: LCM1602_IIC1.D6, I2C_LCD_Display.DB6
  N12: LCM1602_IIC1.D7, I2C_LCD_Display.DB7
  N13: LCM1602_IIC1.A, I2C_LCD_Display.LED+
  N14: LCM1602_IIC1.K, I2C_LCD_Display.LED-
  N15: LCM1602_IIC1.GND, NodeMCU.pin2, NodeMCU.pin_9, NodeMCU.pin_25, NodeMCU.pin_29, Fan_Representer.cathode
  N16: LCM1602_IIC1.VCC, NodeMCU.pin_30
  N17: LCM1602_IIC1.SDA, NodeMCU.pin_13
  N18: LCM1602_IIC1.SCL, NodeMCU.pin_14
  N19: LCM1602_IIC1.LED_A, LCM1602_IIC1.LED_B
  N20: U1.TX0, NodeMCU.pin4
  N21: NodeMCU.pin1, NodeMCU.pin_10, NodeMCU.pin_26
  N22: NodeMCU.pin_15, R1.Pin_1
  N23: Fan_Representer.anode, R1.Pin_0

notes:
  G7 Indoor Unit

custom parts:
  LCM1602 IIC: I2C-Module to use a 1602 or 2004 LCD on with the wire.h libory Serial LCD Modul
  LuaNode32 / ESP32: New Image for LuaNode32 DOIT ESP32 DEVKIT V1. Base parts from LuaNode32 / ESP32 ESP32 based LuaNode32 by G.Noorlander DOIT Esp32 DevKit v1 (30 pins long, 11 pins width) by Werner Rothschopf (modified by vanepp Dec 2018)
